// Logisim project log.circ as structural Verilog
module d_latch (
  input  D,
  input  C,
  output Q
);

  wire and_1_out, and_2_out, nor_1_out, not_1_out;

  not not_1 (not_1_out, D);
  and and_1 (and_1_out, D, C);
  and and_2 (and_2_out, C, not_1_out);
  nor nor_1 (nor_1_out, and_1_out, Q);
  nor nor_2 (Q, nor_1_out, and_2_out);

  // Notes on the sheet:
  //   S
  //   R
  //   S1
  //   R1
endmodule

module d_flipflop (
  input  D,
  input  C,
  output Q
);

  wire d_latch_1_q, not_1_out;

  not not_1 (not_1_out, C);
  d_latch d_latch_1 (.D(D), .C(not_1_out), .Q(d_latch_1_q));
  d_latch d_latch_2 (.D(d_latch_1_q), .C(C), .Q(Q));
endmodule

module Register (
  input  [17:0] Input,
  input  C,
  output [17:0] Output
);

  d_flipflop R0 (.D(Input[0]), .C(C), .Q(Output[0]));
  d_flipflop R1 (.D(Input[1]), .C(C), .Q(Output[1]));
  d_flipflop R2 (.D(Input[2]), .C(C), .Q(Output[2]));
  d_flipflop R3 (.D(Input[3]), .C(C), .Q(Output[3]));
  d_flipflop R4 (.D(Input[4]), .C(C), .Q(Output[4]));
  d_flipflop R5 (.D(Input[5]), .C(C), .Q(Output[5]));
  d_flipflop R6 (.D(Input[6]), .C(C), .Q(Output[6]));
  d_flipflop R7 (.D(Input[7]), .C(C), .Q(Output[7]));
  d_flipflop R8 (.D(Input[8]), .C(C), .Q(Output[8]));
  d_flipflop R9 (.D(Input[9]), .C(C), .Q(Output[9]));
  d_flipflop R10 (.D(Input[10]), .C(C), .Q(Output[10]));
  d_flipflop R12 (.D(Input[12]), .C(C), .Q(Output[12]));
  d_flipflop R11 (.D(Input[11]), .C(C), .Q(Output[11]));
  d_flipflop R13 (.D(Input[13]), .C(C), .Q(Output[13]));
  d_flipflop R14 (.D(Input[14]), .C(C), .Q(Output[14]));
  d_flipflop R15 (.D(Input[15]), .C(C), .Q(Output[15]));
  d_flipflop R16 (.D(Input[16]), .C(C), .Q(Output[16]));
  d_flipflop R17 (.D(Input[17]), .C(C), .Q(Output[17]));
endmodule

module _1_bit_adder (
  input  input1,
  input  input2,
  input  carryin,
  output \output ,
  output carryOut
);

  wire and_1_out, and_2_out, and_3_out, and_4_out, and_5_out, and_6_out, and_7_out, not_1_out, not_2_out,
       not_3_out, not_4_out, not_5_out, not_6_out;

  not not_1 (not_1_out, input1);
  not not_2 (not_2_out, input2);
  not not_3 (not_3_out, input1);
  not not_4 (not_4_out, carryin);
  not not_5 (not_5_out, input2);
  not not_6 (not_6_out, carryin);
  and and_1 (and_1_out, input2, carryin);
  and and_2 (and_2_out, input1, carryin);
  and and_3 (and_3_out, input1, input2);
  and and_4 (and_4_out, not_1_out, not_2_out, carryin);
  and and_5 (and_5_out, not_3_out, input2, not_4_out);
  and and_6 (and_6_out, input1, not_5_out, not_6_out);
  and and_7 (and_7_out, input1, input2, carryin);
  or or_1 (carryOut, and_1_out, and_2_out, and_3_out);
  or or_2 (\output , and_4_out, and_5_out, and_6_out, and_7_out);
endmodule

module Alu (
  input  [17:0] SRC1,
  input  [17:0] SRC2,
  input  [17:0] IMM,
  input  in_4,
  input  [1:0] ALU_Control,
  output [17:0] out_6
);

  wire [17:0] and_1_out, multiplexer_1_out, n18_bit_adder_1_out_3, nand_1_out, nor_1_out;

  Multiplexer #(.width(18), .enable("false")) multiplexer_1 (
    .in0(SRC2), .in1(IMM), .out(multiplexer_1_out), .sel(in_4));
  _18_bit_adder u_18_bit_adder_1 (.in_1(SRC1), .in_2(multiplexer_1_out), .out_3(n18_bit_adder_1_out_3));  // open: out_4
  assign and_1_out = SRC1 & multiplexer_1_out;  // AND_Gate and_1, 18 bits wide
  assign nand_1_out = ~(SRC1 & multiplexer_1_out);  // NAND_Gate nand_1, 18 bits wide
  assign nor_1_out = ~(SRC1 | multiplexer_1_out);  // NOR_Gate nor_1, 18 bits wide
  Multiplexer #(.select(2), .width(18), .enable("false")) multiplexer_2 (
    .in0(and_1_out), .in1(nand_1_out), .in2(nor_1_out), .in3(n18_bit_adder_1_out_3), .out(out_6),
    .sel(ALU_Control));

  // Notes on the sheet:
  //   1 : AND  / 2 : NAND / 3: NOR / 4 : ADD 
endmodule

module _18_bit_adder (
  input  [17:0] in_1,
  input  [17:0] in_2,
  output [17:0] out_3,
  output out_4
);

  wire n1_bit_adder_1_carryout, n1_bit_adder_2_carryout, n1_bit_adder_3_carryout, n1_bit_adder_4_carryout,
       n1_bit_adder_5_carryout, n1_bit_adder_6_carryout, n1_bit_adder_7_carryout, n1_bit_adder_8_carryout,
       n1_bit_adder_9_carryout, n1_bit_adder_10_carryout, n1_bit_adder_11_carryout, n1_bit_adder_12_carryout,
       n1_bit_adder_13_carryout, n1_bit_adder_14_carryout, n1_bit_adder_15_carryout,
       n1_bit_adder_16_carryout, n1_bit_adder_17_carryout;

  _1_bit_adder u_1_bit_adder_1 (
    .input1(in_1[0]), .input2(in_2[0]), .carryin(1'b0), .\output (out_3[0]),
    .carryOut(n1_bit_adder_1_carryout));
  _1_bit_adder u_1_bit_adder_2 (
    .input1(in_1[1]), .input2(in_2[1]), .carryin(n1_bit_adder_1_carryout), .\output (out_3[1]),
    .carryOut(n1_bit_adder_2_carryout));
  _1_bit_adder u_1_bit_adder_3 (
    .input1(in_1[2]), .input2(in_2[2]), .carryin(n1_bit_adder_2_carryout), .\output (out_3[2]),
    .carryOut(n1_bit_adder_3_carryout));
  _1_bit_adder u_1_bit_adder_4 (
    .input1(in_1[3]), .input2(in_2[3]), .carryin(n1_bit_adder_3_carryout), .\output (out_3[3]),
    .carryOut(n1_bit_adder_4_carryout));
  _1_bit_adder u_1_bit_adder_5 (
    .input1(in_1[4]), .input2(in_2[4]), .carryin(n1_bit_adder_4_carryout), .\output (out_3[4]),
    .carryOut(n1_bit_adder_5_carryout));
  _1_bit_adder u_1_bit_adder_6 (
    .input1(in_1[5]), .input2(in_2[5]), .carryin(n1_bit_adder_5_carryout), .\output (out_3[5]),
    .carryOut(n1_bit_adder_6_carryout));
  _1_bit_adder u_1_bit_adder_7 (
    .input1(in_1[6]), .input2(in_2[6]), .carryin(n1_bit_adder_6_carryout), .\output (out_3[6]),
    .carryOut(n1_bit_adder_7_carryout));
  _1_bit_adder u_1_bit_adder_8 (
    .input1(in_1[7]), .input2(in_2[7]), .carryin(n1_bit_adder_7_carryout), .\output (out_3[7]),
    .carryOut(n1_bit_adder_8_carryout));
  _1_bit_adder u_1_bit_adder_9 (
    .input1(in_1[8]), .input2(in_2[8]), .carryin(n1_bit_adder_8_carryout), .\output (out_3[8]),
    .carryOut(n1_bit_adder_9_carryout));
  _1_bit_adder u_1_bit_adder_10 (
    .input1(in_1[9]), .input2(in_2[9]), .carryin(n1_bit_adder_9_carryout), .\output (out_3[9]),
    .carryOut(n1_bit_adder_10_carryout));
  _1_bit_adder u_1_bit_adder_11 (
    .input1(in_1[10]), .input2(in_2[10]), .carryin(n1_bit_adder_10_carryout), .\output (out_3[10]),
    .carryOut(n1_bit_adder_11_carryout));
  _1_bit_adder u_1_bit_adder_12 (
    .input1(in_1[11]), .input2(in_2[11]), .carryin(n1_bit_adder_11_carryout), .\output (out_3[11]),
    .carryOut(n1_bit_adder_12_carryout));
  _1_bit_adder u_1_bit_adder_13 (
    .input1(in_1[12]), .input2(in_2[12]), .carryin(n1_bit_adder_12_carryout), .\output (out_3[12]),
    .carryOut(n1_bit_adder_13_carryout));
  _1_bit_adder u_1_bit_adder_14 (
    .input1(in_1[13]), .input2(in_2[13]), .carryin(n1_bit_adder_13_carryout), .\output (out_3[13]),
    .carryOut(n1_bit_adder_14_carryout));
  _1_bit_adder u_1_bit_adder_15 (
    .input1(in_1[14]), .input2(in_2[14]), .carryin(n1_bit_adder_14_carryout), .\output (out_3[14]),
    .carryOut(n1_bit_adder_15_carryout));
  _1_bit_adder u_1_bit_adder_16 (
    .input1(in_1[15]), .input2(in_2[15]), .carryin(n1_bit_adder_15_carryout), .\output (out_3[15]),
    .carryOut(n1_bit_adder_16_carryout));
  _1_bit_adder u_1_bit_adder_17 (
    .input1(in_1[16]), .input2(in_2[16]), .carryin(n1_bit_adder_16_carryout), .\output (out_3[16]),
    .carryOut(n1_bit_adder_17_carryout));
  _1_bit_adder u_1_bit_adder_18 (
    .input1(in_1[17]), .input2(in_2[17]), .carryin(n1_bit_adder_17_carryout), .\output (out_3[17]),
    .carryOut(out_4));
endmodule
